# Fritzing sketch Connections (saved by Fritzing 0.9.3b)

parts:
  Part1 = 12-Channel 16-bit PWM LED Driver
  Part2 = Arduino Mega 2560 (Rev3)
  R1 = Resistor [tolerance=±5% resistance=220 package="2010 [SMD]"]
  R2 = Resistor [tolerance=±5% resistance=220 package="2010 [SMD]"]

nets:
  VCC: Part1.VCC, Part2.3V3
  GND: Part1.GND, Part2.GND, R2.Pin_1
  N1: Part1.DI, Part2.D11_PWM
  N2: Part1.CI, Part2.D13_PWM
  N3: Part1.V+, R1.Pin_1

notes:
  Power supply
  +
  -
  Note:
  Supply voltage can be 4-17v depends on your requirements.

custom parts:
  12-Channel 16-bit PWM LED Driver: The TLC59711 can control 12 separate channels of 16-bit PWM output. Designed (and ideal) for LED control, this board is not good for driving servos. Only three "SPI" pins are required to send data (our Arduino library shows how to use any digital microcontroller pins). Best of all, the design is completely chainable. As long as there's enough power for all the boards you can chain as many as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
